// Logisim project alu_registry.circ as structural Verilog: 1 circuit, main circuit main
module main (
  input  [7:0] C,
  input  [2:0] slct_C,
  input  [2:0] slct_A,
  input  [2:0] slct_B,
  input  [3:0] slct_op,
  output [7:0] S,
  output S_1_Bit
);

  wire [7:0] registry_file_1_s_a, registry_file_1_s_b;

  registry_file registry_file_1 (
    .slct_c(slct_C), .C(C), .slct_A(slct_A), .slct_B(slct_B), .S_A(registry_file_1_s_a),
    .S_B(registry_file_1_s_b), .S_1_bit(S_1_Bit));
  ALU alu_1 (.A(registry_file_1_s_a), .B(registry_file_1_s_b), .slct(slct_op), .S(S));  // open: Err
endmodule
