// Logisim project squidcpu.circ as structural Verilog: 1 circuit, main circuit main
module main (
);

  wire fetch_decode_1_p1, fetch_decode_1_p3, fetch_decode_1_p4, fetch_decode_1_p5, fetch_decode_1_p6,
       fetch_decode_1_p7, fetch_decode_1_p8, fetch_decode_1_p9, fetch_decode_1_p10, pc_1_p2, pc_1_p7,
       rom_instru_1_p1, rom_instru_1_p2;
  wire [7:0] alu_registry_1_p7, pc_1_p6, ram_data_1_stor_out;

  ram_data ram_data_1 (
    .stor_in(alu_registry_1_p7), .stor_addr(pc_1_p6), .stor(fetch_decode_1_p10),
    .stor_out(ram_data_1_stor_out));
  // rom_instru rom_instru_1: pin names not known; wires that end beside it: rom_instru_1_p1, rom_instru_1_p2
  // fetch_decode fetch_decode_1: pin names not known; wires that end beside it: fetch_decode_1_p1, rom_instru_1_p2, fetch_decode_1_p3, fetch_decode_1_p4, fetch_decode_1_p5, fetch_decode_1_p6, fetch_decode_1_p7, fetch_decode_1_p8, fetch_decode_1_p9, fetch_decode_1_p10
  // pc pc_1: pin names not known; wires that end beside it: ram_data_1_stor_out, pc_1_p2, fetch_decode_1_p1, fetch_decode_1_p3, fetch_decode_1_p5, pc_1_p6, pc_1_p7, rom_instru_1_p1
  // alu_registry alu_registry_1: pin names not known; wires that end beside it: fetch_decode_1_p8, fetch_decode_1_p7, fetch_decode_1_p6, pc_1_p7, fetch_decode_1_p9, fetch_decode_1_p4, alu_registry_1_p7, pc_1_p2
endmodule
